# Fritzing sketch TutoSoudure (saved by Fritzing 1.0.1rc)
stripboards: 1

parts:
  Composant1 = Arduino Uno (Rev3) - ICSP
  LED1 = LED - 5mm [color="Red (633nm)" current=0.030A package="5 mm [THT]"]
  R1 = Resistor [tolerance=±5% resistance=220 package="2010 [SMD]"]

nets:
  N1: Composant1.D13/SCK, Composant1.GND, LED1.anode, R1.Pin_1
  N2: LED1.cathode, R1.Pin_0
