# Fritzing sketch Circuit (saved by Fritzing 1.0.1rc)
breadboards: 1
stripboards: 1

parts:
  LCD1 = LCD screen
  Composant1 = Arduino Uno (Rev3)
  R1 = Resistor [tolerance=±5% power=0.25W resistance=220 package=THT]
  R2 = Rotary Potentiometer (Small) [maximum_resistance=10kΩ knob_status=50% power=0.5W package=THT]
  R3 = Resistor [tolerance=±5% power=0.25W resistance=220 package=THT]
  R4 = Photocell (LDR) [power=0.25W dark_resistance_@0.01lx=300kΩ light_resistance_@100lx=400Ω luminance=10lx package=THT]

nets:
  VSS: LCD1.VSS, LCD1.R/W, LCD1.LED-, Composant1.GND, R3.Pin_1
  VDD: LCD1.VDD, Composant1.5V, R1.Pin_1, R4.pin_0
  N1: LCD1.V0, R2.wiper
  N2: LCD1.RS, Composant1.D12/MISO
  N3: LCD1.E, Composant1.D11_PWM/MOSI
  N4: LCD1.DB4, Composant1.D5_PWM
  N5: LCD1.DB5, Composant1.D4
  N6: LCD1.DB6, Composant1.D3_PWM
  N7: LCD1.DB7, Composant1.D2
  N8: LCD1.LED+, R1.Pin_0
  N9: Composant1.A0, R3.Pin_0, R4.pin_1
